// Logisim project Md.Baker_1911672642_Lab 07 Assignment_Build Full Single Cycle Datapath.circ as structural Verilog: 20 circuits, main circuit main
module main (
);

  AND_Gate_7408 and_gate_7408_1 ();  // open: out_9, out_10, out_11, out_12, in_2, in_3, in_4, in_5, in_6, in_7, in_8, in_1
  NOT_Gate_7404 not_gate_7404_1 ();  // open: out_7, out_8, out_9, out_10, out_11, out_12, in_1, in_2, in_3, in_4, in_5, in_6
  OR_Gate_7432 or_gate_7432_1 ();  // open: out_9, out_10, out_11, out_12, in_2, in_3, in_4, in_5, in_6, in_7, in_8, in_1
  XOR_Gate_7486 xor_gate_7486_1 ();  // open: out_9, out_10, out_11, out_12, in_2, in_3, in_4, in_5, in_6, in_7, in_8, in_1
  MUX_4_1 mux_4_1_1 ();  // open: Q, B, C, D, S0, S1, A
endmodule

module AND_Gate_7408 (
  input  in_1,
  input  in_2,
  input  in_3,
  input  in_4,
  input  in_5,
  input  in_6,
  input  in_7,
  input  in_8,
  output out_9,
  output out_10,
  output out_11,
  output out_12
);

  and and_1 (out_9, in_1, in_2);
  and and_2 (out_10, in_3, in_4);
  and and_3 (out_11, in_5, in_6);
  and and_4 (out_12, in_7, in_8);
endmodule

module OR_Gate_7432 (
  input  in_1,
  input  in_2,
  input  in_3,
  input  in_4,
  input  in_5,
  input  in_6,
  input  in_7,
  input  in_8,
  output out_9,
  output out_10,
  output out_11,
  output out_12
);

  or or_1 (out_9, in_1, in_2);
  or or_2 (out_10, in_3, in_4);
  or or_3 (out_11, in_5, in_6);
  or or_4 (out_12, in_7, in_8);
endmodule

module XOR_Gate_7486 (
  input  in_1,
  input  in_2,
  input  in_3,
  input  in_4,
  input  in_5,
  input  in_6,
  input  in_7,
  input  in_8,
  output out_9,
  output out_10,
  output out_11,
  output out_12
);

  xor xor_1 (out_9, in_1, in_2);
  xor xor_2 (out_10, in_3, in_4);
  xor xor_3 (out_11, in_5, in_6);
  xor xor_4 (out_12, in_7, in_8);
endmodule

module NOT_Gate_7404 (
  input  in_1,
  input  in_2,
  input  in_3,
  input  in_4,
  input  in_5,
  input  in_6,
  output out_7,
  output out_8,
  output out_9,
  output out_10,
  output out_11,
  output out_12
);

  not not_1 (out_7, in_1);
  not not_2 (out_8, in_2);
  not not_3 (out_9, in_3);
  not not_4 (out_10, in_4);
  not not_5 (out_11, in_5);
  not not_6 (out_12, in_6);
endmodule

module MUX_4_1 (
  input  A,
  input  B,
  input  C,
  input  D,
  input  S0,
  input  S1,
  output Q
);

  wire and_1_out, and_2_out, and_3_out, and_4_out, not_1_out, not_2_out;

  not not_1 (not_1_out, S0);
  not not_2 (not_2_out, S1);
  and and_1 (and_1_out, not_2_out, not_1_out, D);
  and and_2 (and_2_out, S1, not_1_out, C);
  and and_3 (and_3_out, not_2_out, S0, B);
  and and_4 (and_4_out, S1, S0, A);
  or or_1 (Q, and_1_out, and_2_out, and_3_out, and_4_out);
endmodule

module Lab_1 (
  input  S0,
  input  A1,
  input  B1,
  input  A2,
  input  B2,
  input  S1,
  output Q1,
  output Q2
);

  wire and_gate_7408_1_out_9, and_gate_7408_1_out_10, not_gate_7404_1_out_7, not_gate_7404_1_out_8,
       or_gate_7432_1_out_9, or_gate_7432_1_out_10, xor_gate_7486_1_out_9, xor_gate_7486_1_out_10;

  AND_Gate_7408 and_gate_7408_1 (
    .out_9(and_gate_7408_1_out_9), .out_10(and_gate_7408_1_out_10), .in_2(B1), .in_3(A2), .in_4(B2), .in_1(A1));  // open: out_11, out_12, in_5, in_6, in_7, in_8
  OR_Gate_7432 or_gate_7432_1 (
    .out_9(or_gate_7432_1_out_9), .out_10(or_gate_7432_1_out_10), .in_2(B1), .in_3(A2), .in_4(B2), .in_1(A1));  // open: out_11, out_12, in_5, in_6, in_7, in_8
  XOR_Gate_7486 xor_gate_7486_1 (
    .out_9(xor_gate_7486_1_out_9), .out_10(xor_gate_7486_1_out_10), .in_2(B1), .in_3(A2), .in_4(B2), .in_1(A1));  // open: out_11, out_12, in_5, in_6, in_7, in_8
  NOT_Gate_7404 not_gate_7404_1 (
    .out_7(not_gate_7404_1_out_7), .out_8(not_gate_7404_1_out_8), .in_1(A1), .in_2(A2));  // open: out_9, out_10, out_11, out_12, in_3, in_4, in_5, in_6
  MUX_DUAL_4_1 mux_dual_4_1_1 (
    .out_11(Q1), .out_12(Q2), .in_9(S0), .in_10(S1), .in_5(not_gate_7404_1_out_8),
    .in_6(xor_gate_7486_1_out_10), .in_7(or_gate_7432_1_out_10), .in_8(and_gate_7408_1_out_10),
    .in_1(not_gate_7404_1_out_7), .in_2(xor_gate_7486_1_out_9), .in_3(or_gate_7432_1_out_9),
    .in_4(and_gate_7408_1_out_9));
endmodule

module MUX_DUAL_4_1 (
  input  in_1,
  input  in_2,
  input  in_3,
  input  in_4,
  input  in_5,
  input  in_6,
  input  in_7,
  input  in_8,
  input  in_9,
  input  in_10,
  output out_11,
  output out_12
);

  MUX_4_1 mux_4_1_1 (.Q(out_11), .B(in_2), .C(in_3), .D(in_4), .S0(in_9), .S1(in_10), .A(in_1));
  MUX_4_1 mux_4_1_2 (.Q(out_12), .B(in_6), .C(in_7), .D(in_8), .S0(in_9), .S1(in_10), .A(in_5));
endmodule

module FA_1_BIT (
  input  A,
  input  B,
  input  C,
  output SUM,
  output CARRY
);

  wire and_gate_7408_1_out_9, and_gate_7408_2_out_9, xor_gate_7486_1_out_9;

  XOR_Gate_7486 xor_gate_7486_1 (
    .out_9(xor_gate_7486_1_out_9), .in_2(B), .in_1(A));  // open: out_10, out_11, out_12, in_3, in_4, in_5, in_6, in_7, in_8
  AND_Gate_7408 and_gate_7408_1 (
    .out_9(and_gate_7408_1_out_9), .in_2(B), .in_1(A));  // open: out_10, out_11, out_12, in_3, in_4, in_5, in_6, in_7, in_8
  AND_Gate_7408 and_gate_7408_2 (
    .out_9(and_gate_7408_2_out_9), .in_2(C), .in_1(xor_gate_7486_1_out_9));  // open: out_10, out_11, out_12, in_3, in_4, in_5, in_6, in_7, in_8
  XOR_Gate_7486 xor_gate_7486_2 (
    .out_9(SUM), .in_2(C), .in_1(xor_gate_7486_1_out_9));  // open: out_10, out_11, out_12, in_3, in_4, in_5, in_6, in_7, in_8
  OR_Gate_7432 or_gate_7432_1 (
    .out_9(CARRY), .in_2(and_gate_7408_1_out_9), .in_1(and_gate_7408_2_out_9));  // open: out_10, out_11, out_12, in_3, in_4, in_5, in_6, in_7, in_8
endmodule

module FA_4 (
  input  A0,
  input  B0,
  input  C,
  input  A1,
  input  B1,
  input  A2,
  input  B2,
  input  A3,
  input  B3,
  output S0,
  output S1,
  output S2,
  output S3,
  output Carry
);

  wire fa_1_bit_1_carry, fa_1_bit_2_carry, fa_1_bit_4_carry;

  FA_1_BIT fa_1_bit_1 (.CARRY(fa_1_bit_1_carry), .SUM(S1), .A(A1), .B(B1), .C(fa_1_bit_4_carry));
  FA_1_BIT fa_1_bit_2 (.CARRY(fa_1_bit_2_carry), .SUM(S2), .A(A2), .B(B2), .C(fa_1_bit_1_carry));
  FA_1_BIT fa_1_bit_3 (.CARRY(Carry), .SUM(S3), .A(A3), .B(B3), .C(fa_1_bit_2_carry));
  FA_1_BIT fa_1_bit_4 (.CARRY(fa_1_bit_4_carry), .SUM(S0), .A(A0), .B(B0), .C(C));
endmodule

module LAB_2 (
  input  A1,
  input  A2,
  input  A3,
  input  A4,
  input  B1,
  input  B2,
  input  B3,
  input  B4,
  input  S0,
  input  S1,
  input  in_11,
  input  Cin,
  output SUM4,
  output SUM3,
  output SUM2,
  output SUM1,
  output Co
);

  wire mux_dual_4_1_1_out_11, mux_dual_4_1_1_out_12, mux_dual_4_1_2_out_11, mux_dual_4_1_2_out_12,
       not_gate_7404_1_out_7, not_gate_7404_1_out_8, not_gate_7404_1_out_9, not_gate_7404_1_out_11,
       not_gate_7404_1_out_12;

  NOT_Gate_7404 not_gate_7404_1 (
    .out_7(not_gate_7404_1_out_7), .out_8(not_gate_7404_1_out_8), .out_9(not_gate_7404_1_out_9),
    .out_11(not_gate_7404_1_out_11), .out_12(not_gate_7404_1_out_12), .in_1(B1), .in_2(B2), .in_3(B3),
    .in_5(in_11), .in_6(B4));  // open: out_10, in_4
  MUX_DUAL_4_1 mux_dual_4_1_1 (
    .out_11(mux_dual_4_1_1_out_11), .out_12(mux_dual_4_1_1_out_12), .in_9(S0), .in_10(S1),
    .in_5(not_gate_7404_1_out_11), .in_6(in_11), .in_7(not_gate_7404_1_out_8), .in_8(B2),
    .in_1(not_gate_7404_1_out_11), .in_2(in_11), .in_3(not_gate_7404_1_out_7), .in_4(B1));
  MUX_DUAL_4_1 mux_dual_4_1_2 (
    .out_11(mux_dual_4_1_2_out_11), .out_12(mux_dual_4_1_2_out_12), .in_9(S0), .in_10(S1),
    .in_5(not_gate_7404_1_out_11), .in_6(in_11), .in_7(not_gate_7404_1_out_12), .in_8(B4),
    .in_1(not_gate_7404_1_out_11), .in_2(in_11), .in_3(not_gate_7404_1_out_9), .in_4(B3));
  FA_4 fa_4_1 (
    .Carry(Co), .S2(SUM3), .S3(SUM4), .S0(SUM1), .S1(SUM2), .A3(A4), .B3(mux_dual_4_1_2_out_12), .A0(A1),
    .B0(mux_dual_4_1_1_out_11), .C(Cin), .A1(A2), .B1(mux_dual_4_1_1_out_12), .A2(A3),
    .B2(mux_dual_4_1_2_out_11));
endmodule

module Lab_3 (
  input  A4,
  input  A3,
  input  A2,
  input  A1,
  input  B4,
  input  B3,
  input  B2,
  input  B1,
  input  in_9,
  input  in_10,
  input  in_11,
  input  in_12,
  output S8,
  output S7,
  output S6,
  output S5,
  output S4,
  output S3,
  output S2,
  output S1
);

  wire A1_B2, A1_B3, A1_B4, A2_B1, A2_B2, A2_B3, A2_B4, A3_B1, A3_B2, A3_B3, A3_B4, A4_B1, A4_B2, A4_B3,
       A4_B4, S1_2, S1_3, S1_4, S1_C, S2_2, S2_3, S2_4, S2_C;

  AND_Gate_7408 and_gate_7408_1 (
    .out_9(S1), .out_10(A1_B2), .out_11(A1_B4), .out_12(A1_B3), .in_2(B1), .in_3(A1), .in_4(B2), .in_5(B4),
    .in_6(A1), .in_7(B3), .in_8(A1), .in_1(A1));
  AND_Gate_7408 and_gate_7408_2 (
    .out_9(A2_B1), .out_10(A2_B2), .out_11(A2_B4), .out_12(A2_B3), .in_2(B1), .in_3(A2), .in_4(B2),
    .in_5(B4), .in_6(A2), .in_7(B3), .in_8(A2), .in_1(A2));
  AND_Gate_7408 and_gate_7408_3 (
    .out_9(A3_B1), .out_10(A3_B2), .out_11(A3_B4), .out_12(A3_B3), .in_2(B1), .in_3(A3), .in_4(B2),
    .in_5(B4), .in_6(A3), .in_7(B3), .in_8(A3), .in_1(A3));
  AND_Gate_7408 and_gate_7408_4 (
    .out_9(A4_B1), .out_10(A4_B2), .out_11(A4_B4), .out_12(A4_B3), .in_2(B1), .in_3(A4), .in_4(B2),
    .in_5(B4), .in_6(A4), .in_7(B3), .in_8(A4), .in_1(A4));
  FA_4 fa_4_1 (
    .Carry(S1_C), .S2(S1_3), .S3(S1_4), .S0(S2), .S1(S1_2), .A3(in_9), .B3(A2_B4), .A0(A1_B2), .B0(A2_B1),
    .C(in_10), .A1(A1_B3), .B1(A2_B2), .A2(A1_B4), .B2(A2_B3));
  FA_4 fa_4_2 (
    .Carry(S2_C), .S2(S2_3), .S3(S2_4), .S0(S3), .S1(S2_2), .A3(S1_C), .B3(A3_B4), .A0(S1_2), .B0(A3_B1),
    .C(in_11), .A1(S1_3), .B1(A3_B2), .A2(S1_4), .B2(A3_B3));
  FA_4 fa_4_3 (
    .Carry(S8), .S2(S6), .S3(S7), .S0(S4), .S1(S5), .A3(S2_C), .B3(A4_B4), .A0(S2_2), .B0(A4_B1), .C(in_12),
    .A1(S2_3), .B1(A4_B2), .A2(S2_4), .B2(A4_B3));

  // Other names for the same wires on the sheet: A1_B1 = S1; S1_1 = S2; S2_1 = S3
endmodule

module Register_16_Bit (
  input  [15:0] in_1,
  input  in_2,
  input  [3:0] in_3,
  input  [3:0] in_4,
  input  [3:0] in_5,
  input  in_6,
  output [15:0] RD1,
  output [15:0] RD2
);

  wire demultiplexer_1_out0, demultiplexer_1_out1, demultiplexer_1_out2, demultiplexer_1_out3,
       demultiplexer_1_out4, demultiplexer_1_out5, demultiplexer_1_out6, demultiplexer_1_out7,
       demultiplexer_1_out8, demultiplexer_1_out9, demultiplexer_1_out10, demultiplexer_1_out11,
       demultiplexer_1_out12, demultiplexer_1_out13, demultiplexer_1_out14, demultiplexer_1_out15;
  wire [15:0] R0_q, R1_q, R2_q, R3_q, R4_q, R5_q, R6_q, R7_q, R8_q, R9_q, R10_q, R11_q, R12_q, R13_q, R14_q,
       R15_q;

  Demultiplexer #(.select(4)) demultiplexer_1 (
    .out0(demultiplexer_1_out0), .out1(demultiplexer_1_out1), .out2(demultiplexer_1_out2),
    .out3(demultiplexer_1_out3), .out4(demultiplexer_1_out4), .out5(demultiplexer_1_out5),
    .out6(demultiplexer_1_out6), .out7(demultiplexer_1_out7), .out8(demultiplexer_1_out8),
    .out9(demultiplexer_1_out9), .out10(demultiplexer_1_out10), .out11(demultiplexer_1_out11),
    .out12(demultiplexer_1_out12), .out13(demultiplexer_1_out13), .out14(demultiplexer_1_out14),
    .out15(demultiplexer_1_out15), .in(in_2), .sel(in_3));
  Register #(.width(16)) R0 (.D(in_1), .en(demultiplexer_1_out0), .Q(R0_q), .clk(in_6));  // open: clr
  Register #(.width(16)) R1 (.D(in_1), .en(demultiplexer_1_out1), .Q(R1_q), .clk(in_6));  // open: clr
  Register #(.width(16)) R2 (.D(in_1), .en(demultiplexer_1_out2), .Q(R2_q), .clk(in_6));  // open: clr
  Register #(.width(16)) R3 (.D(in_1), .en(demultiplexer_1_out3), .Q(R3_q), .clk(in_6));  // open: clr
  Register #(.width(16)) R4 (.D(in_1), .en(demultiplexer_1_out4), .Q(R4_q), .clk(in_6));  // open: clr
  Register #(.width(16)) R5 (.D(in_1), .en(demultiplexer_1_out5), .Q(R5_q), .clk(in_6));  // open: clr
  Register #(.width(16)) R6 (.D(in_1), .en(demultiplexer_1_out6), .Q(R6_q), .clk(in_6));  // open: clr
  Register #(.width(16)) R7 (.D(in_1), .en(demultiplexer_1_out7), .Q(R7_q), .clk(in_6));  // open: clr
  Register #(.width(16)) R8 (.D(in_1), .en(demultiplexer_1_out8), .Q(R8_q), .clk(in_6));  // open: clr
  Register #(.width(16)) R9 (.D(in_1), .en(demultiplexer_1_out9), .Q(R9_q), .clk(in_6));  // open: clr
  Register #(.width(16)) R10 (.D(in_1), .en(demultiplexer_1_out10), .Q(R10_q), .clk(in_6));  // open: clr
  Register #(.width(16)) R11 (.D(in_1), .en(demultiplexer_1_out11), .Q(R11_q), .clk(in_6));  // open: clr
  Register #(.width(16)) R12 (.D(in_1), .en(demultiplexer_1_out12), .Q(R12_q), .clk(in_6));  // open: clr
  Register #(.width(16)) R13 (.D(in_1), .en(demultiplexer_1_out13), .Q(R13_q), .clk(in_6));  // open: clr
  Register #(.width(16)) R14 (.D(in_1), .en(demultiplexer_1_out14), .Q(R14_q), .clk(in_6));  // open: clr
  Register #(.width(16)) R15 (.D(in_1), .en(demultiplexer_1_out15), .Q(R15_q), .clk(in_6));  // open: clr
  Multiplexer #(.select(4), .width(16)) multiplexer_1 (
    .in0(R0_q), .in1(R1_q), .in2(R2_q), .in3(R3_q), .in4(R4_q), .in5(R5_q), .in6(R6_q), .in7(R7_q),
    .in8(R8_q), .in9(R9_q), .in10(R10_q), .in11(R11_q), .in12(R12_q), .in13(R13_q), .in14(R14_q),
    .in15(R15_q), .out(RD1), .sel(in_4));
  Multiplexer #(.select(4), .width(16)) multiplexer_2 (
    .in0(R0_q), .in1(R1_q), .in2(R2_q), .in3(R3_q), .in4(R4_q), .in5(R5_q), .in6(R6_q), .in7(R7_q),
    .in8(R8_q), .in9(R9_q), .in10(R10_q), .in11(R11_q), .in12(R12_q), .in13(R13_q), .in14(R14_q),
    .in15(R15_q), .out(RD2), .sel(in_5));
endmodule

module ALU_1_Bit (
  input  Cin,
  input  A,
  input  B,
  input  Binvert,
  input  [2:0] ALU_OP,
  output Cout,
  output Result
);

  wire adder_1_out, and_1_out, multiplexer_1_out, nand_1_out, nor_1_out, not_1_out, or_1_out, shifter_1_out,
       xor_1_out;

  Multiplexer multiplexer_1 (.in0(B), .in1(not_1_out), .out(multiplexer_1_out), .sel(Binvert));
  not not_1 (not_1_out, B);
  Adder #(.width(1)) adder_1 (.a(A), .b(multiplexer_1_out), .out(adder_1_out), .cin(Cin), .cout(Cout));
  nor nor_1 (nor_1_out, A, B);
  and and_1 (and_1_out, A, B);
  or or_1 (or_1_out, A, B);
  xor xor_1 (xor_1_out, A, B);
  nand nand_1 (nand_1_out, A, B);
  Shifter #(.width(1)) shifter_1 (.in(A), .\dist (B), .out(shifter_1_out));
  Multiplexer #(.select(3)) multiplexer_2 (
    .in0(adder_1_out), .in1(nor_1_out), .in2(and_1_out), .in3(or_1_out), .in4(xor_1_out), .in5(nand_1_out),
    .in6(shifter_1_out), .out(Result), .sel(ALU_OP));  // open: in7
endmodule

module ALU_16_Bit (
  input  Binv,
  input  [2:0] ALU_OP,
  input  Cin,
  input  [15:0] A,
  input  [15:0] B,
  output Zero_Signal,
  output [15:0] Result,
  output Cout
);

  wire alu_1_bit_1_cout, alu_1_bit_2_cout, alu_1_bit_3_cout, alu_1_bit_4_cout, alu_1_bit_5_cout,
       alu_1_bit_6_cout, alu_1_bit_7_cout, alu_1_bit_8_cout, alu_1_bit_9_cout, alu_1_bit_10_cout,
       alu_1_bit_11_cout, alu_1_bit_12_cout, alu_1_bit_13_cout, alu_1_bit_14_cout, alu_1_bit_15_cout;

  ALU_1_Bit alu_1_bit_1 (
    .Result(Result[0]), .Cout(alu_1_bit_1_cout), .A(A[0]), .B(B[0]), .Binvert(Binv), .Cin(Cin),
    .ALU_OP(ALU_OP));
  ALU_1_Bit alu_1_bit_2 (
    .Result(Result[1]), .Cout(alu_1_bit_2_cout), .A(A[1]), .B(B[1]), .Binvert(Binv), .Cin(alu_1_bit_1_cout),
    .ALU_OP(ALU_OP));
  ALU_1_Bit alu_1_bit_3 (
    .Result(Result[2]), .Cout(alu_1_bit_3_cout), .A(A[2]), .B(B[2]), .Binvert(Binv), .Cin(alu_1_bit_2_cout),
    .ALU_OP(ALU_OP));
  ALU_1_Bit alu_1_bit_4 (
    .Result(Result[3]), .Cout(alu_1_bit_4_cout), .A(A[3]), .B(B[3]), .Binvert(Binv), .Cin(alu_1_bit_3_cout),
    .ALU_OP(ALU_OP));
  ALU_1_Bit alu_1_bit_5 (
    .Result(Result[4]), .Cout(alu_1_bit_5_cout), .A(A[4]), .B(B[4]), .Binvert(Binv), .Cin(alu_1_bit_4_cout),
    .ALU_OP(ALU_OP));
  ALU_1_Bit alu_1_bit_6 (
    .Result(Result[5]), .Cout(alu_1_bit_6_cout), .A(A[5]), .B(B[5]), .Binvert(Binv), .Cin(alu_1_bit_5_cout),
    .ALU_OP(ALU_OP));
  ALU_1_Bit alu_1_bit_7 (
    .Result(Result[6]), .Cout(alu_1_bit_7_cout), .A(A[6]), .B(B[6]), .Binvert(Binv), .Cin(alu_1_bit_6_cout),
    .ALU_OP(ALU_OP));
  ALU_1_Bit alu_1_bit_8 (
    .Result(Result[7]), .Cout(alu_1_bit_8_cout), .A(A[7]), .B(B[7]), .Binvert(Binv), .Cin(alu_1_bit_7_cout),
    .ALU_OP(ALU_OP));
  ALU_1_Bit alu_1_bit_9 (
    .Result(Result[8]), .Cout(alu_1_bit_9_cout), .A(A[8]), .B(B[8]), .Binvert(Binv), .Cin(alu_1_bit_8_cout),
    .ALU_OP(ALU_OP));
  ALU_1_Bit alu_1_bit_10 (
    .Result(Result[9]), .Cout(alu_1_bit_10_cout), .A(A[9]), .B(B[9]), .Binvert(Binv), .Cin(alu_1_bit_9_cout),
    .ALU_OP(ALU_OP));
  ALU_1_Bit alu_1_bit_11 (
    .Result(Result[10]), .Cout(alu_1_bit_11_cout), .A(A[10]), .B(B[10]), .Binvert(Binv),
    .Cin(alu_1_bit_10_cout), .ALU_OP(ALU_OP));
  ALU_1_Bit alu_1_bit_12 (
    .Result(Result[11]), .Cout(alu_1_bit_12_cout), .A(A[11]), .B(B[11]), .Binvert(Binv),
    .Cin(alu_1_bit_11_cout), .ALU_OP(ALU_OP));
  ALU_1_Bit alu_1_bit_13 (
    .Result(Result[12]), .Cout(alu_1_bit_13_cout), .A(A[12]), .B(B[12]), .Binvert(Binv),
    .Cin(alu_1_bit_12_cout), .ALU_OP(ALU_OP));
  ALU_1_Bit alu_1_bit_14 (
    .Result(Result[13]), .Cout(alu_1_bit_14_cout), .A(A[13]), .B(B[13]), .Binvert(Binv),
    .Cin(alu_1_bit_13_cout), .ALU_OP(ALU_OP));
  ALU_1_Bit alu_1_bit_15 (
    .Result(Result[14]), .Cout(alu_1_bit_15_cout), .A(A[14]), .B(B[14]), .Binvert(Binv),
    .Cin(alu_1_bit_14_cout), .ALU_OP(ALU_OP));
  ALU_1_Bit alu_1_bit_16 (
    .Result(Result[15]), .Cout(Cout), .A(A[15]), .B(B[15]), .Binvert(Binv), .Cin(alu_1_bit_15_cout),
    .ALU_OP(ALU_OP));
  nor nor_1 (Zero_Signal, Result[0], Result[1], Result[2], Result[3], Result[4], Result[5], Result[6], Result[7], Result[8], Result[9], Result[10], Result[11], Result[12], Result[13], Result[14], Result[15]);
endmodule

module R_Type (
  input  in_1,
  input  in_2,
  input  in_3,
  input  [15:0] in_4,
  input  in_5,
  input  [2:0] in_6,
  output [3:0] OpCode,
  output [3:0] RS,
  output [3:0] RT,
  output [3:0] RD,
  output [15:0] Data1,
  output [15:0] Data2,
  output out_13,
  output [15:0] out_14
);

  wire clock_1_out;
  wire [15:0] adder_1_out, PC_q;

  Counter #(.max('hffff), .width(16)) PC (
    .D(adder_1_out), .Q(PC_q), .clk(clock_1_out));  // open: load, count, carry, up, clr
  Clock clock_1 (.out(clock_1_out));
  ROM #(.addrWidth(16), .dataWidth(16)) rom_1 (.addr(PC_q), .data({OpCode, RS, RT, RD}));
  Adder #(.width(16)) adder_1 (.a(PC_q), .b(16'h1), .out(adder_1_out));  // open: cin, cout
  Register_16_Bit register_16_bit_1 (
    .RD1(Data1), .RD2(Data2), .in_4(RS), .in_5(RT), .in_1(out_14), .in_6(clock_1_out), .in_2(in_5), .in_3(RD));
  ALU_16_Bit alu_16_bit_1 (
    .Cout(in_3), .Result(out_14), .Zero_Signal(out_13), .B(Data2), .A(Data1), .Cin(in_1), .Binv(in_2),
    .ALU_OP(in_6));

  // Notes on the sheet:
  //   Clock
  //   contents of rom_1 (hex, n*v repeats v):
  //   234
endmodule

module I_Type (
  input  in_1,
  input  in_2,
  input  in_3,
  input  [15:0] in_4,
  input  in_5,
  input  [2:0] in_6,
  output [3:0] OpCode,
  output [3:0] RS,
  output [3:0] RT,
  output [3:0] Imm,
  output [15:0] Data1,
  output [15:0] Data2,
  output out_13,
  output [15:0] out_14
);

  wire clock_1_out;
  wire [15:0] adder_1_out, PC_q;

  Counter #(.max('hffff), .width(16)) PC (
    .D(adder_1_out), .Q(PC_q), .clk(clock_1_out));  // open: load, count, carry, up, clr
  Clock clock_1 (.out(clock_1_out));
  ROM #(.addrWidth(16), .dataWidth(16)) rom_1 (.addr(PC_q), .data({OpCode, RS, RT, Imm}));
  Adder #(.width(16)) adder_1 (.a(PC_q), .b(16'h1), .out(adder_1_out));  // open: cin, cout
  assign Data2 = {{12{1'b0}}, Imm};  // Bit_Extender bit_extender_1
  Register_16_Bit register_16_bit_1 (
    .RD1(Data1), .in_4(RS), .in_1(out_14), .in_6(clock_1_out), .in_2(in_5), .in_3(RT));  // open: RD2, in_5
  ALU_16_Bit alu_16_bit_1 (
    .Cout(in_3), .Result(out_14), .Zero_Signal(out_13), .B(Data2), .A(Data1), .Cin(in_1), .Binv(in_2),
    .ALU_OP(in_6));

  // Notes on the sheet:
  //   Clock
  //   contents of rom_1 (hex, n*v repeats v):
  //   149
  //   Addi $R1 $R4 9
  //   0   1  4  9  
endmodule

module Load_Type (
  input  in_1,
  input  in_2,
  input  in_3,
  input  in_4,
  input  in_5,
  input  [2:0] in_6,
  output [3:0] OpCode,
  output [3:0] RS,
  output [3:0] RT,
  output [3:0] Imm,
  output [15:0] Data1,
  output [15:0] Data2,
  output out_13,
  output [15:0] out_14
);

  wire clock_1_out;
  wire [15:0] adder_1_out, PC_q, ram_1_dout;

  Counter #(.max('hffff), .width(16)) PC (
    .D(adder_1_out), .Q(PC_q), .clk(clock_1_out));  // open: load, count, carry, up, clr
  Clock clock_1 (.out(clock_1_out));
  ROM #(.addrWidth(16), .dataWidth(16)) rom_1 (.addr(PC_q), .data({OpCode, RS, RT, Imm}));
  Adder #(.width(16)) adder_1 (.a(PC_q), .b(16'h1), .out(adder_1_out));  // open: cin, cout
  assign Data2 = {{12{1'b0}}, Imm};  // Bit_Extender bit_extender_1
  Register_16_Bit register_16_bit_1 (
    .RD1(Data1), .in_4(RS), .in_1(ram_1_dout), .in_6(clock_1_out), .in_2(in_4), .in_3(RT));  // open: RD2, in_5
  ALU_16_Bit alu_16_bit_1 (
    .Cout(in_3), .Result(out_14), .Zero_Signal(out_13), .B(Data2), .A(Data1), .Cin(in_1), .Binv(in_2),
    .ALU_OP(in_6));
  RAM #(.addrWidth(16), .dataWidth(16), .trigger("high"), .\type ("nonvolatile")) ram_1 (
    .addr(out_14), .oe(in_5), .clk(clock_1_out), .dout(ram_1_dout));  // open: we, din

  // Notes on the sheet:
  //   Clock
  //   5    1    8   9
  //   contents of rom_1 (hex, n*v repeats v):
  //   5189
  //   LW $R1($R8)offset
endmodule

module Store_Type (
  input  in_1,
  input  in_2,
  input  in_3,
  input  in_4,
  input  in_5,
  input  [2:0] in_6,
  output [3:0] OpCode,
  output [3:0] RS,
  output [3:0] RT,
  output [3:0] Imm,
  output [15:0] Data1,
  output [15:0] Data2,
  output out_13,
  output [15:0] out_14
);

  wire clock_1_out;
  wire [15:0] adder_1_out, PC_q, register_16_bit_1_rd2;

  Counter #(.max('hffff), .width(16)) PC (
    .D(adder_1_out), .Q(PC_q), .clk(clock_1_out));  // open: load, count, carry, up, clr
  Clock clock_1 (.out(clock_1_out));
  ROM #(.addrWidth(16), .dataWidth(16)) rom_1 (.addr(PC_q), .data({OpCode, RS, RT, Imm}));
  Adder #(.width(16)) adder_1 (.a(PC_q), .b(16'h1), .out(adder_1_out));  // open: cin, cout
  assign Data2 = {{12{1'b0}}, Imm};  // Bit_Extender bit_extender_1
  Register_16_Bit register_16_bit_1 (
    .RD1(Data1), .RD2(register_16_bit_1_rd2), .in_4(RS), .in_5(RT), .in_6(clock_1_out), .in_2(in_4));  // open: in_1, in_3
  ALU_16_Bit alu_16_bit_1 (
    .Cout(in_3), .Result(out_14), .Zero_Signal(out_13), .B(Data2), .A(Data1), .Cin(in_1), .Binv(in_2),
    .ALU_OP(in_6));
  RAM #(.addrWidth(16), .dataWidth(16), .trigger("high"), .\type ("nonvolatile")) ram_1 (
    .addr(out_14), .we(in_5), .clk(clock_1_out));  // open: oe, din, dout

  // Notes on the sheet:
  //   Clock
  //   SW $R1 $R2 4
  //   contents of rom_1 (hex, n*v repeats v):
  //   124
  //   mem R1+4 =R2
  //   0 1 2 4 
  //   0000    0001     0100   
endmodule

module Lab_7_Assignment (
  input  Write_Enb,
  input  Reg_dst,
  input  ALU_src,
  input  [2:0] ALU_op,
  input  Sub,
  input  Ram_to_Reg,
  input  Store_enb,
  input  Load_enb,
  input  Cout,
  output [3:0] RS,
  output [3:0] RT,
  output [3:0] OpCode,
  output [3:0] Write_Reg,
  output [15:0] Data1,
  output [15:0] Data2,
  output out_16,
  output [15:0] out_17,
  output [15:0] Data_For_Store
);

  wire clock_1_out;
  wire [3:0] multiplexer_1_out;
  wire [15:0] adder_1_out, alu_16_bit_1_result, bit_extender_1_out, PC_q, ram_1_dout;

  Counter #(.max('hffff), .width(16)) PC (
    .D(adder_1_out), .Q(PC_q), .clk(clock_1_out));  // open: load, count, carry, up, clr
  Clock clock_1 (.out(clock_1_out));
  ROM #(.addrWidth(16), .dataWidth(16)) rom_1 (.addr(PC_q), .data({OpCode, RS, RT, Write_Reg}));
  Adder #(.width(16)) adder_1 (.a(PC_q), .b(16'h1), .out(adder_1_out));  // open: cin, cout
  Multiplexer #(.width(4)) multiplexer_1 (.in0(Write_Reg), .in1(RT), .out(multiplexer_1_out), .sel(Reg_dst));
  assign bit_extender_1_out = {{12{Write_Reg[3]}}, Write_Reg};  // Bit_Extender bit_extender_1
  Register_16_Bit register_16_bit_1 (
    .RD1(Data1), .RD2(Data_For_Store), .in_4(RS), .in_5(RT), .in_1(out_17), .in_6(clock_1_out),
    .in_2(Write_Enb), .in_3(multiplexer_1_out));
  Multiplexer #(.width(16)) multiplexer_2 (.in0(Data_For_Store), .in1(bit_extender_1_out), .out(Data2), .sel(ALU_src));
  ALU_16_Bit alu_16_bit_1 (
    .Cout(Cout), .Result(alu_16_bit_1_result), .Zero_Signal(out_16), .B(Data2), .A(Data1), .Cin(Sub),
    .Binv(Sub), .ALU_OP(ALU_op));
  RAM #(.addrWidth(16), .dataWidth(16), .trigger("high"), .\type ("nonvolatile")) ram_1 (
    .addr(alu_16_bit_1_result), .we(Store_enb), .oe(Load_enb), .din(Data_For_Store), .dout(ram_1_dout));
  Multiplexer #(.width(16)) multiplexer_3 (.in0(alu_16_bit_1_result), .in1(ram_1_dout), .out(out_17), .sel(Ram_to_Reg));

  // Notes on the sheet:
  //   Clock
  //   contents of rom_1 (hex, n*v repeats v):
  //   124
  //   For Jump
  //   Read_Reg1
  //   Read_Reg2
  //   Result_Val
endmodule
